// Digital circuit selenay.batibay_PRELAB1.dig as structural Verilog
module selenay_batibay_PRELAB1 (
  input  [3:0] in,
  output sign,
  output [3:0] out
);

  wire dipswitch_1_out, dipswitch_2_out;
  wire [0:0] xor_4_out;
  wire [2:0] xor_1_out;

  DipSwitch dipswitch_1 (.out(dipswitch_1_out));
  xor xor_1 (xor_1_out[0], in[0], in[3]);
  xor xor_2 (xor_1_out[1], in[1], in[3]);
  xor xor_3 (xor_1_out[2], in[2], in[3]);
  xor xor_4 (xor_4_out[0], in[3], dipswitch_1_out);
  Add #(.Bits(3)) add_1 (.a(xor_1_out), .b({2'b00, xor_4_out[0]}), .c_i(dipswitch_2_out), .s(out[2:0]), .c_o(out[3]));
  DipSwitch dipswitch_2 (.out(dipswitch_2_out));

  assign sign = in[3];
endmodule
