// Digital circuit selenay.batibay_hw1 (1).dig as structural Verilog
module selenay_batibay_hw1__1 (
  input  A0,
  input  A1,
  input  B0,
  input  B1,
  input  in_6,
  output [3:0] M
);

  wire [1:0] and_1_out;
  wire [2:1] and_3_out;

  and and_1 (and_1_out[0], A0, B0);
  and and_2 (and_1_out[1], B0, A1);
  and and_3 (and_3_out[1], A0, B1);
  and and_4 (and_3_out[2], B1, A1);
  Add #(.Bits(3)) add_1 (.a({1'b0, and_1_out}), .b({and_3_out, 1'b0}), .c_i(in_6), .s(M[2:0]), .c_o(M[3]));
endmodule
