// Digital circuit selenay.batibay_lab1.dig as structural Verilog
module selenay_batibay_lab1 (
  input  in_1,
  input  in_2,
  input  in_3,
  input  in_4,
  input  in_5,
  input  in_6,
  input  in_7,
  input  in_8
);

  wire dipswitch_1_out;
  wire [3:0] unsignedbcd6_1_p1, unsignedbcd6_1_p3, unsignedbcd_1_p1, unsignedbcd_1_p3, unsignedbcd_2_p1,
       unsignedbcd_2_p3;
  wire [4:0] unsignedbcd6_1_p2;

  Seven_Seg_Hex seven_seg_hex_1 (.d(unsignedbcd_1_p1), .dp(1'b0));
  Seven_Seg_Hex seven_seg_hex_2 (.d(unsignedbcd_1_p3), .dp(1'b0));
  // unsignedBCD unsignedbcd_1: pin names not known; wires that end beside it: unsignedbcd_1_p1, {in_5, in_6, in_7, in_8}, unsignedbcd_1_p3
  Seven_Seg_Hex seven_seg_hex_3 (.d(unsignedbcd_2_p1), .dp(1'b0));
  Seven_Seg_Hex seven_seg_hex_4 (.d(unsignedbcd_2_p3), .dp(1'b0));
  // unsignedBCD unsignedbcd_2: pin names not known; wires that end beside it: unsignedbcd_2_p1, {in_1, in_2, in_3, in_4}, unsignedbcd_2_p3
  Seven_Seg_Hex seven_seg_hex_5 (.d(unsignedbcd6_1_p1), .dp(1'b0));
  Seven_Seg_Hex seven_seg_hex_6 (.d(unsignedbcd6_1_p3), .dp(1'b0));
  // unsignedBCD6 unsignedbcd6_1: pin names not known; wires that end beside it: unsignedbcd6_1_p1, unsignedbcd6_1_p2, unsignedbcd6_1_p3
  Add #(.Bits(5)) add_1 (
    .a({in_5, in_6, in_7, in_8, 1'b0}), .b({1'b0, in_1, in_2, in_3, in_4}), .c_i(dipswitch_1_out),
    .s(unsignedbcd6_1_p2));  // open: c_o
  DipSwitch dipswitch_1 (.out(dipswitch_1_out));

  // Notes on the sheet:
  //   2x
  //   +
  //   =
endmodule
