// Digital circuit selenay.batibay_lab2.dig as structural Verilog
module selenay_batibay_lab2 (
  input  I3,
  input  I2,
  input  I1,
  input  I0,
  output MSB,
  output out_2,
  output out_3,
  output LSB
);

  wire and_1_out, and_2_out, and_3_out, and_4_out, and_5_out, and_6_out, and_7_out, and_8_out, not_1_out,
       not_2_out, not_3_out, not_4_out;

  not not_1 (not_1_out, I3);
  not not_2 (not_2_out, I2);
  not not_3 (not_3_out, I1);
  not not_4 (not_4_out, I0);
  and and_1 (and_1_out, I2, I0);
  and and_2 (and_2_out, I2, I1);
  and and_3 (and_3_out, not_1_out, not_3_out, not_4_out);
  and and_4 (and_4_out, I3, not_3_out, I0);
  and and_5 (and_5_out, I2, not_3_out);
  or or_1 (out_3, I2, I1);
  and and_6 (and_6_out, not_2_out, not_3_out);
  and and_7 (and_7_out, not_2_out, not_4_out);
  and and_8 (and_8_out, I2, I1, I0);
  or or_2 (MSB, I3, and_1_out, and_2_out);
  or or_3 (out_2, and_3_out, and_4_out, and_5_out);
  or or_4 (LSB, and_6_out, and_7_out, and_8_out);
endmodule
