// Digital circuit selenay.batibay_lab4 (1).dig as structural Verilog
module selenay_batibay_lab4__1 (
  input  _1Hz
);

  wire and_1_out, d_ff_1_nq, d_ff_1_q, not_1_out, undriven_2;
  wire [3:0] and_2_out, and_3_out, and_4_out, and_5_out, and_6_out, undriven;

  D_FF d_ff_1 (.D(d_ff_1_nq), .Q(d_ff_1_q), .nQ(d_ff_1_nq));  // open: C
  not not_1 (not_1_out, and_2_out[0]);
  and and_1 (and_1_out, undriven_2, d_ff_1_q);
  assign and_2_out = and_6_out & and_5_out & and_4_out & and_3_out;  // And and_2, 4 bits wide
  and and_3 (and_3_out[0], ~1'b0, ~undriven[0]);  // And
  and and_4 (and_4_out[0], undriven[1], ~1'b0);  // And
  and and_5 (and_5_out[0], undriven[2], ~1'b0);  // And
  and and_6 (and_6_out[0], ~1'b0, ~undriven[3]);  // And
  Seven_Seg seven_seg_1 (.g(undriven[0]), .dp(1'b0));  // open: a, b, c, d, e, f
  Seven_Seg seven_seg_2 (.dp(1'b0));  // open: a, b, c, d, e, f, g
  // Pins of 1 and 4 bits meet at and_6_out
  // Pins of 1 and 4 bits meet at and_5_out
  // Pins of 1 and 4 bits meet at and_4_out
  // Pins of 1 and 4 bits meet at and_3_out
  // Pins of 1 and 4 bits meet at and_2_out
  // Pins of 1 and 4 bits meet at undriven
endmodule
